# Fritzing sketch Monitor IoT Temperatura e Umidade (saved by Fritzing 0.9.3b)
breadboards: 1

parts:
  Componente2 = Barometric Pressure Sensor - BMP180 Breakout (GY-68)
  U1 = ESP8266 NodeMCU LoLin module
  Componente3 = LCD1602-I2C
  YwRobot_Power_Supply1 = YwRobot Breadboard Power Supply [part_number=545043]
  CONN1 = USB connector [package=THT]  # not connected

nets:
  N1: Componente2.VCC, U1.D2, Componente3.SDA
  N2: Componente2.GND, U1.D1, Componente3.SCL
  GND: Componente2.SCL, U1.GND, Componente3.GND, YwRobot_Power_Supply1.GND#13, YwRobot_Power_Supply1.GND#14
  N3: Componente2.SDA, Componente3.VCC, YwRobot_Power_Supply1.VCC#9, YwRobot_Power_Supply1.VCC#10
  N4: YwRobot_Power_Supply1.VCC#5, YwRobot_Power_Supply1.VCC#6
  N5: YwRobot_Power_Supply1.GND#11, YwRobot_Power_Supply1.GND#12

custom parts:
  Barometric Pressure Sensor - BMP180 Breakout (GY-68): This is a simple breakout board for the BMP180, a high-precision, low-power barometric pressure sensor made by Bosch Sensortec. The range of measurement is from 300hPa to 1100hPa. The sensor can be supplied with voltage ranging from 1.8V to 3.6V. Operating temperature range is -40 to +85 °C. This particular breakout board (or perhaps the configuration) is produced by Shenzhen Keep Power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
  ESP8266 NodeMCU LoLin module: ESP8266 based NodeMCU
  LCD1602-I2C: A standard character display, usually with 2x16 characters. Comes in many colors with LCM1602 IIC attached.
  YwRobot Breadboard Power Supply: The YwRobot Breadboard Power Supply (MB-V2) has two power rails; they can be 5V or 3V3. Power to the module can be provided through the female USB socket or through the A10 (female) 2.1mm power jack.
